// Logisim project CPU.circ as structural Verilog: 16 circuits, main circuit main
module main (
  input  in_1,
  input  in_2,
  input  in_3,
  input  in_4,
  input  in_5,
  input  in_6,
  input  in_7,
  input  in_8,
  input  Debug
);

  wire A0, A1, A2, A3, A4, A5, A6, A7, A8, AI, B1, B2, B3, B4, B5, B6, B7, B8, bcd_1_out_2, bcd_1_out_3,
       bcd_1_out_4, bcd_1_out_5, BI, C, CE, CF, Clear, clock_1_out, CO, controlled_buffer_3_out, CY, EO, FI,
       HLT, I0, II, IR1, IR2, IR3, IR4, IR5, IR6, IR7, IR8, J, MAI, nor_1_out, not_1_out, not_2_out,
       not_3_out, OI, or_1_out, R, RI, RO, splitter_1_out_2, splitter_1_out_3, splitter_1_out_4,
       splitter_1_out_5, splitter_1_out_6, splitter_1_out_7, splitter_1_out_8, splitter_1_out_9,
       splitter_1_out_10, splitter_1_out_11, splitter_1_out_12, splitter_1_out_13, splitter_1_out_14,
       splitter_1_out_15, splitter_1_out_16, splitter_1_out_17, Step_out, SU, ZF;
  wire [2:0] INS_STEP;
  wire [3:0] ADR, bcd_1_hundreds, bcd_1_ones, bcd_1_tens, bcd_1_thousands, counter_2_q;
  wire [7:0] ALU_OUT, BUS, controlled_buffer_1_out, OUT;
  wire [15:0] MICRO_CODE;

  LED led_1 (.in(BUS[5]));
  LED led_2 (.in(BUS[7]));
  LED led_3 (.in(BUS[6]));
  Pull_Resistor pull_resistor_1 (.node(BUS[7]));
  Pull_Resistor pull_resistor_2 (.node(BUS[5]));
  Pull_Resistor pull_resistor_3 (.node(BUS[6]));
  LED led_4 (.in(BUS[3]));
  LED led_5 (.in(BUS[2]));
  LED led_6 (.in(BUS[4]));
  LED led_7 (.in(BUS[1]));
  Pull_Resistor pull_resistor_4 (.node(BUS[2]));
  Pull_Resistor pull_resistor_5 (.node(BUS[3]));
  Pull_Resistor pull_resistor_6 (.node(BUS[4]));
  Pull_Resistor pull_resistor_7 (.node(BUS[1]));
  LED led_8 (.in(BUS[0]));
  Pull_Resistor pull_resistor_8 (.node(BUS[0]));
  Register register_1 (
    .Write(A0), .Load(AI), .CLK(C), .D0(BUS[0]), .D1(BUS[1]), .D2(BUS[2]), .D3(BUS[3]), .D4(BUS[4]),
    .D5(BUS[5]), .D6(BUS[6]), .D7(BUS[7]), .Q0(BUS[0]), .Q1(BUS[1]), .Q2(BUS[2]), .Q3(BUS[3]), .Q4(BUS[4]),
    .Q5(BUS[5]), .Q6(BUS[6]), .Q7(BUS[7]), .S0(A1), .S1(A2), .S2(A3), .S3(A4), .S4(A5), .S5(A6), .S6(A7),
    .S7(A8), .Clear(Clear));
  Register register_2 (
    .Write(1'b0), .Load(BI), .CLK(C), .D0(BUS[0]), .D1(BUS[1]), .D2(BUS[2]), .D3(BUS[3]), .D4(BUS[4]),
    .D5(BUS[5]), .D6(BUS[6]), .D7(BUS[7]), .Q0(BUS[0]), .Q1(BUS[1]), .Q2(BUS[2]), .Q3(BUS[3]), .Q4(BUS[4]),
    .Q5(BUS[5]), .Q6(BUS[6]), .Q7(BUS[7]), .S0(B1), .S1(B2), .S2(B3), .S3(B4), .S4(B5), .S5(B6), .S6(B7),
    .S7(B8), .Clear(Clear));
  Register register_3 (
    .Write(1'b0), .Load(OI), .CLK(C), .D0(BUS[0]), .D1(BUS[1]), .D2(BUS[2]), .D3(BUS[3]), .D4(BUS[4]),
    .D5(BUS[5]), .D6(BUS[6]), .D7(BUS[7]), .Q0(BUS[0]), .Q1(BUS[1]), .Q2(BUS[2]), .Q3(BUS[3]), .Q4(BUS[4]),
    .Q5(BUS[5]), .Q6(BUS[6]), .Q7(BUS[7]), .S0(OUT[0]), .S1(OUT[1]), .S2(OUT[2]), .S3(OUT[3]), .S4(OUT[4]),
    .S5(OUT[5]), .S6(OUT[6]), .S7(OUT[7]), .Clear(Clear));
  Register register_4 (
    .Write(I0), .Load(II), .CLK(C), .D0(BUS[0]), .D1(BUS[1]), .D2(BUS[2]), .D3(BUS[3]), .D4(BUS[4]),
    .D5(BUS[5]), .D6(BUS[6]), .D7(BUS[7]), .Q0(BUS[0]), .Q1(BUS[1]), .Q2(BUS[2]), .Q3(BUS[3]), .S0(IR1),
    .S1(IR2), .S2(IR3), .S3(IR4), .S4(IR5), .S5(IR6), .S6(IR7), .S7(IR8), .Clear(Clear));  // open: Q4, Q5, Q6, Q7
  LED led_9 (.in(IR3));
  LED led_10 (.in(IR4));
  LED led_11 (.in(IR2));
  Hex_Digit_Display hex_digit_display_1 (.value(bcd_1_thousands), .dp(bcd_1_out_2));
  Hex_Digit_Display hex_digit_display_2 (.value(bcd_1_hundreds), .dp(bcd_1_out_3));
  assign controlled_buffer_1_out = RI ? BUS : 8'bz;  // Controlled_Buffer controlled_buffer_1
  LED led_12 (.in(IR1));
  LED led_13 (.in(IR8));
  Hex_Digit_Display hex_digit_display_3 (.value(bcd_1_ones), .dp(bcd_1_out_5));
  BCD bcd_1 (
    .Value(OUT), .Thousands(bcd_1_thousands), .Hundreds(bcd_1_hundreds), .Ones(bcd_1_ones),
    .Tens(bcd_1_tens), .out_2(bcd_1_out_2), .out_3(bcd_1_out_3), .out_4(bcd_1_out_4), .out_5(bcd_1_out_5));
  Hex_Digit_Display hex_digit_display_4 (.value(bcd_1_tens), .dp(bcd_1_out_4));
  not not_1 (not_1_out, RI);
  _4BitRegister u_4bitregister_1 (
    .Write(1'b0), .Load(MAI), .CLK(C), .D0(BUS[0]), .D1(BUS[1]), .D2(BUS[2]), .D3(BUS[3]), .Q0(BUS[0]),
    .S0(ADR[0]), .Q1(BUS[1]), .S1(ADR[1]), .Q2(BUS[2]), .S2(ADR[2]), .Q3(BUS[3]), .S3(ADR[3]), .Clear(Clear));
  LED led_14 (.in(IR7));
  LED led_15 (.in(IR6));
  LED led_16 (.in(IR5));
  RAM #(.addrWidth(4), .Select("high"), .simpleMode("false")) ram_1 (
    .addr(ADR), .data(controlled_buffer_1_out), .sel(1'b1), .clk(C), .ld(not_1_out), .clr(1'b0));
  LED led_17 (.in(ADR[2]));
  LED led_18 (.in(ADR[3]));
  Button Step (.out(Step_out));
  Button Reset (.out(Clear));
  assign BUS = RO ? controlled_buffer_1_out : 8'bz;  // Controlled_Buffer controlled_buffer_2
  LED led_19 (.in(ADR[0]));
  LED led_20 (.in(ADR[1]));
  ROM #(.addrWidth(9), .dataWidth(16), .Select("low")) rom_1 (
    .addr({ZF, CF, IR8, IR7, IR6, IR5, INS_STEP}), .data(MICRO_CODE), .sel(1'b0));
  assign controlled_buffer_3_out = Debug ? Step_out : 1'bz;  // Controlled_Buffer controlled_buffer_3
  assign controlled_buffer_3_out = not_2_out ? clock_1_out : 1'bz;  // Controlled_Buffer controlled_buffer_4
  not not_2 (not_2_out, Debug);
  Clock clock_1 (.out(clock_1_out));
  Pull_Resistor pull_resistor_9 (.node(MAI));
  Pull_Resistor pull_resistor_10 (.node(HLT));
  LED led_21 (.in(HLT));
  LED led_22 (.in(MAI));
  LargerBuffer largerbuffer_1 (
    .E(1'b1), .D0(splitter_1_out_2), .D1(splitter_1_out_3), .D2(splitter_1_out_4), .D3(splitter_1_out_5),
    .D4(splitter_1_out_6), .D5(splitter_1_out_7), .D6(splitter_1_out_8), .D7(splitter_1_out_9), .Q0(HLT),
    .Q1(MAI), .Q2(RI), .Q3(RO), .Q4(I0), .Q5(II), .Q6(AI), .Q7(A0));
  not not_3 (not_3_out, C);
  and and_1 (C, controlled_buffer_3_out, ~Clear, ~HLT);  // AND_Gate
  AddSub addsub_1 (
    .Co(CY), .Cin(SU), .A8(A8), .A7(A7), .A6(A6), .A5(A5), .A4(A4), .A3(A3), .A2(A2), .A1(A1),
    .S8(ALU_OUT[7]), .S7(ALU_OUT[6]), .S6(ALU_OUT[5]), .S5(ALU_OUT[4]), .S4(ALU_OUT[3]), .S3(ALU_OUT[2]),
    .S2(ALU_OUT[1]), .S1(ALU_OUT[0]), .B8(B8), .B7(B7), .B6(B6), .B5(B5), .B4(B4), .B3(B3), .B2(B2), .B1(B1));
  Pull_Resistor pull_resistor_11 (.node(I0));
  Pull_Resistor pull_resistor_12 (.node(RI));
  Pull_Resistor pull_resistor_13 (.node(RO));
  LED led_23 (.in(RI));
  LED led_24 (.in(RO));
  LED led_25 (.in(I0));
  LED led_26 (.in(INS_STEP[0]));
  LED led_27 (.in(INS_STEP[2]));
  LED led_28 (.in(INS_STEP[1]));
  Counter #(.width(3), .max('h7), .behavior("old")) counter_1 (
    .load(1'b0), .D(3'b000), .count(1'b1), .Q(INS_STEP), .clk(not_3_out), .clr(or_1_out), .preset(1'b0));  // open: carry
  or or_1 (or_1_out, R, Clear);
  Tri_StateBuffers tri_statebuffers_1 (
    .E(EO), .D0(ALU_OUT[0]), .D1(ALU_OUT[1]), .D2(ALU_OUT[2]), .D3(ALU_OUT[3]), .D4(ALU_OUT[4]),
    .D5(ALU_OUT[5]), .D6(ALU_OUT[6]), .D7(ALU_OUT[7]), .Q0(BUS[0]), .Q1(BUS[1]), .Q2(BUS[2]), .Q3(BUS[3]),
    .Q4(BUS[4]), .Q5(BUS[5]), .Q6(BUS[6]), .Q7(BUS[7]));
  Pull_Resistor pull_resistor_14 (.node(A0));
  Pull_Resistor pull_resistor_15 (.node(AI));
  Pull_Resistor pull_resistor_16 (.node(II));
  LED led_29 (.in(II));
  LED led_30 (.in(AI));
  LED led_31 (.in(A0));
  Demultiplexer #(.select(3), .disabled(0), .enable("false")) demultiplexer_1 (
    .out5(R), .in(1'b1), .sel(INS_STEP));  // open: out0, out1, out2, out3, out4, out6, out7
  nor nor_1 (nor_1_out, ALU_OUT[7], ALU_OUT[6], ALU_OUT[5], ALU_OUT[4], ALU_OUT[3], ALU_OUT[2], ALU_OUT[1], ALU_OUT[0]);
  Pull_Resistor pull_resistor_17 (.node(EO));
  Pull_Resistor pull_resistor_18 (.node(SU));
  LED led_32 (.in(EO));
  LED led_33 (.in(SU));
  LargerBuffer largerbuffer_2 (
    .E(1'b1), .D0(splitter_1_out_10), .D1(splitter_1_out_11), .D2(splitter_1_out_12), .D3(splitter_1_out_13),
    .D4(splitter_1_out_14), .D5(splitter_1_out_15), .D6(splitter_1_out_16), .D7(splitter_1_out_17), .Q0(EO),
    .Q1(SU), .Q2(BI), .Q3(OI), .Q4(CE), .Q5(CO), .Q6(J), .Q7(FI));
  Splitter splitter_1 (
    .Clear(MICRO_CODE), .out_2(splitter_1_out_2), .out_3(splitter_1_out_3), .out_4(splitter_1_out_4),
    .out_5(splitter_1_out_5), .out_6(splitter_1_out_6), .out_7(splitter_1_out_7), .out_8(splitter_1_out_8),
    .out_9(splitter_1_out_9), .out_10(splitter_1_out_10), .out_11(splitter_1_out_11),
    .out_12(splitter_1_out_12), .out_13(splitter_1_out_13), .out_14(splitter_1_out_14),
    .out_15(splitter_1_out_15), .out_16(splitter_1_out_16), .out_17(splitter_1_out_17));
  Tri_StateBuffers tri_statebuffers_2 (
    .E(CO), .D0(1'b0), .D1(1'b0), .D2(1'b0), .D3(1'b0), .D4(counter_2_q[3]), .D5(counter_2_q[2]),
    .D6(counter_2_q[1]), .D7(counter_2_q[0]), .Q0(BUS[7]), .Q1(BUS[6]), .Q2(BUS[5]), .Q3(BUS[4]),
    .Q4(BUS[3]), .Q5(BUS[2]), .Q6(BUS[1]), .Q7(BUS[0]));
  LED led_34 (.in(counter_2_q[3]));
  Counter #(.width(4), .max('hf), .behavior("old")) counter_2 (
    .load(J), .D(BUS[3:0]), .count(CE), .Q(counter_2_q), .clk(C), .clr(Clear));  // open: carry, preset
  Pull_Resistor pull_resistor_19 (.node(CE));
  Pull_Resistor pull_resistor_20 (.node(OI));
  Pull_Resistor pull_resistor_21 (.node(BI));
  LED led_35 (.in(BI));
  LED led_36 (.in(OI));
  LED led_37 (.in(CE));
  LED led_38 (.in(OUT[5]));
  LED led_39 (.in(OUT[4]));
  LED led_40 (.in(OUT[7]));
  LED led_41 (.in(OUT[6]));
  _2BitRegister u_2bitregister_1 (
    .Write(1'b0), .Load(FI), .CLK(C), .D0(nor_1_out), .D1(CY), .Q0(nor_1_out), .S0(ZF), .Clear(Clear),
    .Q1(CY), .S1(CF));
  LED Carry (.in(CF));
  LED led_42 (.in(counter_2_q[0]));
  LED led_43 (.in(counter_2_q[1]));
  LED led_44 (.in(counter_2_q[2]));
  Pull_Resistor pull_resistor_22 (.node(CO));
  Pull_Resistor pull_resistor_23 (.node(J));
  Pull_Resistor pull_resistor_24 (.node(FI));
  LED led_45 (.in(J));
  LED led_46 (.in(CO));
  LED led_47 (.in(FI));
  LED led_48 (.in(OUT[1]));
  LED led_49 (.in(OUT[2]));
  LED led_50 (.in(OUT[3]));
  LED led_51 (.in(OUT[0]));
  LED Zero (.in(ZF));
  Hex_Digit_Display hex_digit_display_5 (.value({in_1, in_2, in_3, in_4}));  // open: dp
  Hex_Digit_Display hex_digit_display_6 (.value({in_5, in_6, in_7, in_8}));  // open: dp

  // Other names for the same wires on the sheet: OUT1 = OUT[0]; OUT2 = OUT[1]; OUT3 = OUT[2]; OUT4 = OUT[3];
  //   OUT5 = OUT[4]; OUT6 = OUT[5]; OUT7 = OUT[6]; OUT8 = OUT[7]

  // Notes on the sheet:
  //   BUS
  //   A
  //   B
  //   OUT
  //   INS
  //   Data
  //   Instruction Register
  //   RAM
  //   Memory Address Register
  //   ADR
  //   Microcode ROM
  //   Instruction
  //   contents of rom_1 (hex, n*v repeats v):
  //   2002 1028 6*0 2002 1028 12 48 4*0 2002 1028 12 408 8140 0 0 0 2002 1028 12 408 8340 0 0 0 2002 1028
  //   12 84 4*0 2002 1028 50 5*0 2002 1028 4010 5*0 2002 1028 6*0 2002 1028 6*0 2002 1028 6*0 2002 1028
  //   6*0 2002 1028 6*0 2002 1028 6*0 2002 1028 6*0 2002 1028 880 5*0 2002 1028 1 5*0 2002 1028 6*0 2002
  //   1028 12 48 4*0 2002 1028 12 408 8140 0 0 0 2002 1028 12 408 8340 0 0 0 2002 1028 12 84 4*0 2002 1028
  //   50 5*0 2002 1028 4010 5*0 2002 1028 4010 5*0 2002 1028 6*0 2002 1028 6*0 2002 1028 6*0 2002 1028 6*0
  //   2002 1028 6*0 2002 1028 6*0 2002 1028 880 5*0 2002 1028 1 5*0 2002 1028 6*0 2002 1028 12 48 4*0 2002
  //   1028 12 408 8140 0 0 0 2002 1028 12 408 8340 0 0 0 2002 1028 12 84 4*0 2002 1028 50 5*0 2002 1028
  //   4010 5*0 2002 1028 6*0 2002 1028 4010 5*0 2002 1028 6*0 2002 1028 6*0 2002 1028 6*0 2002 1028 6*0
  //   2002 1028 6*0 2002 1028 880 5*0 2002 1028 1 5*0 2002 1028 6*0 2002 1028 12 48 4*0 2002 1028 12 408
  //   8140 0 0 0 2002 1028 12 408 8340 0 0 0 2002 1028 12 84 4*0 2002 1028 50 5*0 2002 1028 4010 5*0 2002
  //   1028 4010 5*0 2002 1028 4010 5*0 2002 1028 6*0 2002 1028 6*0 2002 1028 6*0 2002 1028 6*0 2002 1028
  //   6*0 2002 1028 880 5*0 2002 1028 1
  //   Clock
  //   ALU
  //   MC. Instruction Counter
  //   Control Ward
  //   Flags Register
  //   Program Counter
  //   BIN OUT
endmodule

module SingleRegister (
  input  CLK,
  input  D,
  input  Clear,
  output Out,
  output Inverted_Out
);

  D_Flip_Flop d_ff_1 (.clk(CLK), .D(D), .Q(Out), .Qn(Inverted_Out), .preset(1'b0), .reset(Clear));
endmodule

module Register (
  input  Write,
  input  Load,
  input  CLK,
  input  D0,
  input  Clear,
  input  D1,
  input  D2,
  input  D3,
  input  D4,
  input  D5,
  input  D6,
  input  D7,
  output Q0,
  output S0,
  output Q1,
  output S1,
  output Q2,
  output S2,
  output Q3,
  output S3,
  output Q4,
  output S4,
  output Q5,
  output S5,
  output Q6,
  output S6,
  output Q7,
  output S7
);

  wire and_1_out, and_2_out, and_3_out, and_4_out, and_5_out, and_6_out, and_7_out, and_8_out, and_9_out,
       and_10_out, and_11_out, and_12_out, and_13_out, and_14_out, and_15_out, and_16_out, not_1_out,
       not_2_out, not_3_out, not_4_out, not_5_out, not_6_out, not_7_out, not_8_out, or_1_out, or_2_out,
       or_3_out, or_4_out, or_5_out, or_6_out, or_7_out, or_8_out;

  not not_1 (not_1_out, Load);
  Pull_Resistor pull_resistor_1 (.node(D0));
  not not_2 (not_2_out, Load);
  Pull_Resistor pull_resistor_2 (.node(D1));
  not not_3 (not_3_out, Load);
  Pull_Resistor pull_resistor_3 (.node(D2));
  not not_4 (not_4_out, Load);
  Pull_Resistor pull_resistor_4 (.node(D3));
  not not_5 (not_5_out, Load);
  Pull_Resistor pull_resistor_5 (.node(D4));
  not not_6 (not_6_out, Load);
  Pull_Resistor pull_resistor_6 (.node(D5));
  not not_7 (not_7_out, Load);
  Pull_Resistor pull_resistor_7 (.node(D6));
  not not_8 (not_8_out, Load);
  Pull_Resistor pull_resistor_8 (.node(D7));
  and and_1 (and_1_out, S0, not_1_out);
  and and_2 (and_2_out, Load, D0);
  and and_3 (and_3_out, S1, not_2_out);
  and and_4 (and_4_out, Load, D1);
  and and_5 (and_5_out, S2, not_3_out);
  and and_6 (and_6_out, Load, D2);
  and and_7 (and_7_out, S3, not_4_out);
  and and_8 (and_8_out, Load, D3);
  and and_9 (and_9_out, S4, not_5_out);
  and and_10 (and_10_out, Load, D4);
  and and_11 (and_11_out, S5, not_6_out);
  and and_12 (and_12_out, Load, D5);
  and and_13 (and_13_out, S6, not_7_out);
  and and_14 (and_14_out, Load, D6);
  and and_15 (and_15_out, S7, not_8_out);
  and and_16 (and_16_out, Load, D7);
  or or_1 (or_1_out, and_1_out, and_2_out);
  SingleRegister singleregister_1 (.CLK(CLK), .D(or_1_out), .Out(S0), .Clear(Clear));  // open: Inverted_Out
  SingleRegister singleregister_2 (.CLK(CLK), .D(or_2_out), .Out(S1), .Clear(Clear));  // open: Inverted_Out
  or or_2 (or_2_out, and_3_out, and_4_out);
  or or_3 (or_3_out, and_5_out, and_6_out);
  SingleRegister singleregister_3 (.CLK(CLK), .D(or_3_out), .Out(S2), .Clear(Clear));  // open: Inverted_Out
  or or_4 (or_4_out, and_7_out, and_8_out);
  SingleRegister singleregister_4 (.CLK(CLK), .D(or_4_out), .Out(S3), .Clear(Clear));  // open: Inverted_Out
  or or_5 (or_5_out, and_9_out, and_10_out);
  SingleRegister singleregister_5 (.CLK(CLK), .D(or_5_out), .Out(S4), .Clear(Clear));  // open: Inverted_Out
  or or_6 (or_6_out, and_11_out, and_12_out);
  SingleRegister singleregister_6 (.CLK(CLK), .D(or_6_out), .Out(S5), .Clear(Clear));  // open: Inverted_Out
  or or_7 (or_7_out, and_13_out, and_14_out);
  SingleRegister singleregister_7 (.CLK(CLK), .D(or_7_out), .Out(S6), .Clear(Clear));  // open: Inverted_Out
  SingleRegister singleregister_8 (.CLK(CLK), .D(or_8_out), .Out(S7), .Clear(Clear));  // open: Inverted_Out
  or or_8 (or_8_out, and_15_out, and_16_out);
  assign Q0 = Write ? S0 : 1'bz;  // Controlled_Buffer controlled_buffer_1
  assign Q1 = Write ? S1 : 1'bz;  // Controlled_Buffer controlled_buffer_2
  assign Q2 = Write ? S2 : 1'bz;  // Controlled_Buffer controlled_buffer_3
  assign Q3 = Write ? S3 : 1'bz;  // Controlled_Buffer controlled_buffer_4
  assign Q4 = Write ? S4 : 1'bz;  // Controlled_Buffer controlled_buffer_5
  assign Q5 = Write ? S5 : 1'bz;  // Controlled_Buffer controlled_buffer_6
  assign Q6 = Write ? S6 : 1'bz;  // Controlled_Buffer controlled_buffer_7
  assign Q7 = Write ? S7 : 1'bz;  // Controlled_Buffer controlled_buffer_8
endmodule

module Tri_StateBuffers (
  input  E,
  input  D0,
  input  D1,
  input  D2,
  input  D3,
  input  D4,
  input  D5,
  input  D6,
  input  D7,
  output Q0,
  output Q1,
  output Q2,
  output Q3,
  output Q4,
  output Q5,
  output Q6,
  output Q7
);

  assign Q0 = E ? D0 : 1'bz;  // Controlled_Buffer controlled_buffer_1
  assign Q1 = E ? D1 : 1'bz;  // Controlled_Buffer controlled_buffer_2
  assign Q2 = E ? D2 : 1'bz;  // Controlled_Buffer controlled_buffer_3
  assign Q3 = E ? D3 : 1'bz;  // Controlled_Buffer controlled_buffer_4
  assign Q4 = E ? D4 : 1'bz;  // Controlled_Buffer controlled_buffer_5
  assign Q5 = E ? D5 : 1'bz;  // Controlled_Buffer controlled_buffer_6
  assign Q6 = E ? D6 : 1'bz;  // Controlled_Buffer controlled_buffer_7
  assign Q7 = E ? D7 : 1'bz;  // Controlled_Buffer controlled_buffer_8
endmodule

module HalfAdder (
  input  A,
  input  B,
  output S,
  output C
);

  xor xor_1 (S, A, B);
  and and_1 (C, A, B);
endmodule

module FullAdder (
  input  CIN,
  input  A,
  input  B,
  output S,
  output COUT
);

  wire halfadder_1_c, halfadder_1_s, halfadder_2_c;

  HalfAdder halfadder_1 (.A(A), .B(B), .S(halfadder_1_s), .C(halfadder_1_c));
  HalfAdder halfadder_2 (.A(halfadder_1_s), .B(CIN), .S(S), .C(halfadder_2_c));
  or or_1 (COUT, halfadder_2_c, halfadder_1_c);
endmodule

module AddSub (
  input  B8,
  input  B7,
  input  B6,
  input  B5,
  input  B4,
  input  B3,
  input  B2,
  input  B1,
  input  Cin,
  input  A8,
  input  A7,
  input  A6,
  input  A5,
  input  A4,
  input  A3,
  input  A2,
  input  A1,
  output Co,
  output S8,
  output S7,
  output S6,
  output S5,
  output S4,
  output S3,
  output S2,
  output S1
);

  wire fulladder_2_cout, fulladder_3_cout, fulladder_4_cout, fulladder_5_cout, fulladder_6_cout,
       fulladder_7_cout, fulladder_8_cout, xor_1_out, xor_2_out, xor_3_out, xor_4_out, xor_5_out, xor_6_out,
       xor_7_out, xor_8_out;

  xor xor_1 (xor_1_out, B8, Cin);
  FullAdder fulladder_1 (.CIN(fulladder_2_cout), .A(xor_1_out), .B(A8), .S(S8), .COUT(Co));
  xor xor_2 (xor_2_out, B7, Cin);
  FullAdder fulladder_2 (.CIN(fulladder_3_cout), .A(xor_2_out), .B(A7), .S(S7), .COUT(fulladder_2_cout));
  xor xor_3 (xor_3_out, B6, Cin);
  FullAdder fulladder_3 (.CIN(fulladder_4_cout), .A(xor_3_out), .B(A6), .S(S6), .COUT(fulladder_3_cout));
  xor xor_4 (xor_4_out, B5, Cin);
  FullAdder fulladder_4 (.CIN(fulladder_5_cout), .A(xor_4_out), .B(A5), .S(S5), .COUT(fulladder_4_cout));
  xor xor_5 (xor_5_out, B4, Cin);
  FullAdder fulladder_5 (.CIN(fulladder_6_cout), .A(xor_5_out), .B(A4), .S(S4), .COUT(fulladder_5_cout));
  xor xor_6 (xor_6_out, B3, Cin);
  FullAdder fulladder_6 (.CIN(fulladder_7_cout), .A(xor_6_out), .B(A3), .S(S3), .COUT(fulladder_6_cout));
  xor xor_7 (xor_7_out, B2, Cin);
  FullAdder fulladder_7 (.CIN(fulladder_8_cout), .A(xor_7_out), .B(A2), .S(S2), .COUT(fulladder_7_cout));
  xor xor_8 (xor_8_out, B1, Cin);
  FullAdder fulladder_8 (.CIN(Cin), .A(xor_8_out), .B(A1), .S(S1), .COUT(fulladder_8_cout));

  // Notes on the sheet:
  //   Co: pull=down
endmodule

module Ram (
  input  [7:0] Data,
  input  Store,
  input  [3:0] Address,
  input  Clock,
  output [7:0] Data_2
);

  wire C_out, not_1_out;

  assign Data_2 = Store ? Data : 8'bz;  // Controlled_Buffer controlled_buffer_1
  not not_1 (not_1_out, Store);
  RAM #(.addrWidth(4), .Select("high"), .simpleMode("false")) ram_1 (
    .addr(Address), .data(Data_2), .sel(1'b1), .clk(Clock), .ld(not_1_out), .clr(C_out));
  Button C (.out(C_out));
endmodule

module _4BitRegister (
  input  Write,
  input  Load,
  input  CLK,
  input  D0,
  input  Clear,
  input  D1,
  input  D2,
  input  D3,
  output Q0,
  output S0,
  output Q1,
  output S1,
  output Q2,
  output S2,
  output Q3,
  output S3
);

  wire and_1_out, and_2_out, and_3_out, and_4_out, and_5_out, and_6_out, and_7_out, and_8_out, not_1_out,
       not_2_out, not_3_out, not_4_out, or_1_out, or_2_out, or_3_out, or_4_out;

  not not_1 (not_1_out, Load);
  Pull_Resistor pull_resistor_1 (.node(D0));
  not not_2 (not_2_out, Load);
  Pull_Resistor pull_resistor_2 (.node(D1));
  not not_3 (not_3_out, Load);
  Pull_Resistor pull_resistor_3 (.node(D2));
  not not_4 (not_4_out, Load);
  Pull_Resistor pull_resistor_4 (.node(D3));
  and and_1 (and_1_out, S0, not_1_out);
  and and_2 (and_2_out, Load, D0);
  and and_3 (and_3_out, S1, not_2_out);
  and and_4 (and_4_out, Load, D1);
  and and_5 (and_5_out, S2, not_3_out);
  and and_6 (and_6_out, Load, D2);
  and and_7 (and_7_out, S3, not_4_out);
  and and_8 (and_8_out, Load, D3);
  or or_1 (or_1_out, and_1_out, and_2_out);
  SingleRegister singleregister_1 (.CLK(CLK), .D(or_1_out), .Out(S0), .Clear(Clear));  // open: Inverted_Out
  or or_2 (or_2_out, and_3_out, and_4_out);
  SingleRegister singleregister_2 (.CLK(CLK), .D(or_2_out), .Out(S1), .Clear(Clear));  // open: Inverted_Out
  SingleRegister singleregister_3 (.CLK(CLK), .D(or_3_out), .Out(S2), .Clear(Clear));  // open: Inverted_Out
  or or_3 (or_3_out, and_5_out, and_6_out);
  SingleRegister singleregister_4 (.CLK(CLK), .D(or_4_out), .Out(S3), .Clear(Clear));  // open: Inverted_Out
  or or_4 (or_4_out, and_7_out, and_8_out);
  assign Q0 = Write ? S0 : 1'bz;  // Controlled_Buffer controlled_buffer_1
  assign Q1 = Write ? S1 : 1'bz;  // Controlled_Buffer controlled_buffer_2
  assign Q2 = Write ? S2 : 1'bz;  // Controlled_Buffer controlled_buffer_3
  assign Q3 = Write ? S3 : 1'bz;  // Controlled_Buffer controlled_buffer_4
endmodule

module _3DigitDisplay (
);

  Hex_Digit_Display hex_digit_display_1 (.dp(1'b0));  // open: value
  Hex_Digit_Display hex_digit_display_2 (.dp(1'b0));  // open: value
  BCD bcd_1 ();  // open: Value, Thousands, Hundreds, Ones, Tens, out_2, out_3, out_4, out_5
  Hex_Digit_Display hex_digit_display_3 (.dp(1'b0));  // open: value
  Hex_Digit_Display hex_digit_display_4 (.dp(1'b0));  // open: value
endmodule

module Programmer (
  input  in_1,
  input  in_2,
  input  in_3,
  input  in_4,
  input  in_5,
  input  in_6,
  input  in_7,
  input  in_8,
  input  in_9,
  input  in_10,
  input  in_11,
  input  in_12,
  input  in_13,
  input  in_14,
  input  in_15,
  input  in_16,
  input  in_17,
  input  in_18,
  input  in_19,
  input  in_20,
  input  in_21,
  input  in_22,
  input  in_23,
  input  in_24,
  input  in_25,
  input  in_26,
  input  in_27,
  input  in_28,
  input  in_29,
  input  in_30,
  input  in_31,
  input  in_32,
  input  in_33,
  input  in_34,
  input  C,
  input  Z
);

  wire not_1_out;
  wire [15:0] controlled_buffer_1_out;

  Hex_Digit_Display hex_digit_display_1 (.value({in_1, in_2, in_3, in_4}));  // open: dp
  Hex_Digit_Display hex_digit_display_2 (.value({in_5, in_6, in_7, in_8}));  // open: dp
  assign controlled_buffer_1_out = in_25 ? {in_24, in_23, in_22, in_21, in_20, in_19, in_18, in_17, in_16, in_15, in_14, in_13, in_12, in_11, in_10, in_9} : 16'bz;  // Controlled_Buffer controlled_buffer_1
  not not_1 (not_1_out, in_25);
  RAM #(.addrWidth(9), .dataWidth(16), .Select("high"), .simpleMode("false")) ram_1 (
    .addr({Z, C, in_28, in_29, in_30, in_31, in_32, in_33, in_34}), .data(controlled_buffer_1_out),
    .sel(1'b1), .clk(in_27), .ld(not_1_out), .clr(in_26));
endmodule

module Splitter (
  input  [15:0] Clear,
  output out_2,
  output out_3,
  output out_4,
  output out_5,
  output out_6,
  output out_7,
  output out_8,
  output out_9,
  output out_10,
  output out_11,
  output out_12,
  output out_13,
  output out_14,
  output out_15,
  output out_16,
  output out_17
);


  assign out_2 = Clear[0];
  assign out_3 = Clear[1];
  assign out_4 = Clear[2];
  assign out_5 = Clear[3];
  assign out_6 = Clear[4];
  assign out_7 = Clear[5];
  assign out_8 = Clear[6];
  assign out_9 = Clear[7];
  assign out_10 = Clear[8];
  assign out_11 = Clear[9];
  assign out_12 = Clear[10];
  assign out_13 = Clear[11];
  assign out_14 = Clear[12];
  assign out_15 = Clear[13];
  assign out_16 = Clear[14];
  assign out_17 = Clear[15];
endmodule

module LargerBuffer (
  input  E,
  input  D0,
  input  D1,
  input  D2,
  input  D3,
  input  D4,
  input  D5,
  input  D6,
  input  D7,
  output Q0,
  output Q1,
  output Q2,
  output Q3,
  output Q4,
  output Q5,
  output Q6,
  output Q7
);

  assign Q0 = E ? D0 : 1'bz;  // Controlled_Buffer controlled_buffer_1
  assign Q1 = E ? D1 : 1'bz;  // Controlled_Buffer controlled_buffer_2
  assign Q2 = E ? D2 : 1'bz;  // Controlled_Buffer controlled_buffer_3
  assign Q3 = E ? D3 : 1'bz;  // Controlled_Buffer controlled_buffer_4
  assign Q4 = E ? D4 : 1'bz;  // Controlled_Buffer controlled_buffer_5
  assign Q5 = E ? D5 : 1'bz;  // Controlled_Buffer controlled_buffer_6
  assign Q6 = E ? D6 : 1'bz;  // Controlled_Buffer controlled_buffer_7
  assign Q7 = E ? D7 : 1'bz;  // Controlled_Buffer controlled_buffer_8
endmodule

module _2BitRegister (
  input  Write,
  input  Load,
  input  CLK,
  input  D0,
  input  Clear,
  input  D1,
  output Q0,
  output S0,
  output Q1,
  output S1
);

  wire and_1_out, and_2_out, and_3_out, and_4_out, not_1_out, not_2_out, or_1_out, or_2_out;

  not not_1 (not_1_out, Load);
  Pull_Resistor pull_resistor_1 (.node(D0));
  not not_2 (not_2_out, Load);
  Pull_Resistor pull_resistor_2 (.node(D1));
  and and_1 (and_1_out, S0, not_1_out);
  and and_2 (and_2_out, Load, D0);
  and and_3 (and_3_out, S1, not_2_out);
  and and_4 (and_4_out, Load, D1);
  or or_1 (or_1_out, and_1_out, and_2_out);
  SingleRegister singleregister_1 (.CLK(CLK), .D(or_1_out), .Out(S0), .Clear(Clear));  // open: Inverted_Out
  or or_2 (or_2_out, and_3_out, and_4_out);
  SingleRegister singleregister_2 (.CLK(CLK), .D(or_2_out), .Out(S1), .Clear(Clear));  // open: Inverted_Out
  assign Q0 = Write ? S0 : 1'bz;  // Controlled_Buffer controlled_buffer_1
  assign Q1 = Write ? S1 : 1'bz;  // Controlled_Buffer controlled_buffer_2
endmodule

module BCD (
  input  [7:0] Value,
  output out_2,
  output out_3,
  output out_4,
  output out_5,
  output [3:0] Ones,
  output [3:0] Thousands,
  output [3:0] Tens,
  output [3:0] Hundreds
);

  wire add3_1_s0, add3_1_s1, add3_1_s2, add3_1_s3, add3_2_s0, add3_2_s1, add3_2_s2, add3_4_s0, add3_4_s1,
       add3_4_s2, add3_4_s3, add3_5_s0, add3_5_s1, add3_5_s2, add3_5_s3, add3_6_s0, add3_6_s1, add3_6_s2,
       add3_6_s3;

  add3 add3_1 (
    .S0(add3_1_s0), .S1(add3_1_s1), .S2(add3_1_s2), .S3(add3_1_s3), .A3(1'b0), .A2(Value[7]), .A1(Value[6]),
    .A0(Value[5]));
  add3 add3_2 (
    .S0(add3_2_s0), .S1(add3_2_s1), .S2(add3_2_s2), .S3(Hundreds[1]), .A3(1'b0), .A2(add3_1_s3),
    .A1(add3_4_s3), .A0(add3_5_s3));
  add3 add3_3 (
    .S0(Tens[1]), .S1(Tens[2]), .S2(Tens[3]), .S3(Hundreds[0]), .A3(add3_2_s2), .A2(add3_2_s1),
    .A1(add3_2_s0), .A0(add3_6_s3));
  add3 add3_4 (
    .S0(add3_4_s0), .S1(add3_4_s1), .S2(add3_4_s2), .S3(add3_4_s3), .A3(add3_1_s2), .A2(add3_1_s1),
    .A1(add3_1_s0), .A0(Value[4]));
  add3 add3_5 (
    .S0(add3_5_s0), .S1(add3_5_s1), .S2(add3_5_s2), .S3(add3_5_s3), .A3(add3_4_s2), .A2(add3_4_s1),
    .A1(add3_4_s0), .A0(Value[3]));
  add3 add3_6 (
    .S0(add3_6_s0), .S1(add3_6_s1), .S2(add3_6_s2), .S3(add3_6_s3), .A3(add3_5_s2), .A2(add3_5_s1),
    .A1(add3_5_s0), .A0(Value[2]));
  add3 add3_7 (
    .S0(Ones[1]), .S1(Ones[2]), .S2(Ones[3]), .S3(Tens[0]), .A3(add3_6_s2), .A2(add3_6_s1), .A1(add3_6_s0),
    .A0(Value[1]));

  assign Hundreds[3:2] = 2'b00;
  assign Ones[0] = Value[0];
  assign out_2 = 1'b0;
  assign out_3 = 1'b0;
  assign out_4 = 1'b0;
  assign out_5 = 1'b0;
  assign Thousands = 4'b0000;
endmodule

module add3 (
  input  A3,
  input  A2,
  input  A1,
  input  A0,
  output S0,
  output S1,
  output S2,
  output S3
);

  wire comparator_1_lt, fulladder_1_s, fulladder_2_cout, fulladder_2_s, fulladder_3_cout, fulladder_3_s,
       fulladder_4_cout, fulladder_4_s, not_1_out;

  FullAdder fulladder_1 (.CIN(fulladder_2_cout), .A(1'b0), .B(A3), .S(fulladder_1_s));  // open: COUT
  FullAdder fulladder_2 (.CIN(fulladder_3_cout), .A(1'b0), .B(A2), .S(fulladder_2_s), .COUT(fulladder_2_cout));
  FullAdder fulladder_3 (.CIN(fulladder_4_cout), .A(1'b1), .B(A1), .S(fulladder_3_s), .COUT(fulladder_3_cout));
  FullAdder fulladder_4 (.CIN(1'b0), .A(1'b1), .B(A0), .S(fulladder_4_s), .COUT(fulladder_4_cout));
  assign S0 = comparator_1_lt ? A0 : 1'bz;  // Controlled_Buffer controlled_buffer_1
  assign S1 = comparator_1_lt ? A1 : 1'bz;  // Controlled_Buffer controlled_buffer_2
  assign S2 = comparator_1_lt ? A2 : 1'bz;  // Controlled_Buffer controlled_buffer_3
  assign S3 = comparator_1_lt ? A3 : 1'bz;  // Controlled_Buffer controlled_buffer_4
  Comparator #(.width(4), .mode("unsigned")) comparator_1 (
    .a({A3, A2, A1, A0}), .b(4'b0101), .lt(comparator_1_lt));  // open: gt, eq
  assign S0 = not_1_out ? fulladder_4_s : 1'bz;  // Controlled_Buffer controlled_buffer_5
  assign S1 = not_1_out ? fulladder_3_s : 1'bz;  // Controlled_Buffer controlled_buffer_6
  not not_1 (not_1_out, comparator_1_lt);
  assign S2 = not_1_out ? fulladder_2_s : 1'bz;  // Controlled_Buffer controlled_buffer_7
  assign S3 = not_1_out ? fulladder_1_s : 1'bz;  // Controlled_Buffer controlled_buffer_8
endmodule
